// Logisim project My Sap.circ as structural Verilog: 1 circuit, main circuit main
module main (
);

  wire A_IN, A_OUT, ADDR_IN, ALU_C, ALU_CLC, ALU_OUT, ALU_S, ALU_STC, ALU_SUB, ALU_Z, and_1_out, and_2_out,
       and_4_out, and_5_out, and_6_out, and_7_out, and_8_out, and_9_out, and_10_out, and_11_out, B_IN, B_OUT,
       C, C_OUT, CLK, decoder_1_out0, decoder_1_out1, decoder_1_out3, decoder_1_out4, decoder_1_out5,
       decoder_1_out6, decoder_1_out7, DISP_IN, FLAG_INV, HALT, HEX, IR_IN, JMP, MODE_out, nor_1_out,
       not_1_out, OCTAL, or_1_out, or_3_out, or_4_out, OSC_out, PC_IN, PC_INC, PC_OUT, RAM_IN, RAM_OUT,
       RESET, RUN, RUN_out, S, S_OUT, SIGNED, STEP_out, T2, T_RESET, TMP_IN, TMP_OUT, UNSIGNED, xor_1_out,
       xor_2_out, xor_3_out, Z, Z_OUT;
  wire [1:0] MODE;
  wire [2:0] T_STATE;
  wire [3:0] rom_2_data_2, rom_2_data_4;
  wire [7:0] A_BUS, adder_1_out, controlled_buffer_7_out, counter_1_q, IR_REG, multiplexer_1_out, ram_1_data,
       register_1_q, register_4_q, register_5_q, register_6_q, subtractor_1_out, W_BUS;
  wire [7:4] rom_2_data_3, rom_2_data_5;
  wire [8:8] adder_1_cout, subtractor_1_bout;
  wire [15:0] rom_2_data;

  Button u_RESET (.out(RESET));
  Button u_RUN (.out(RUN_out));
  Button STEP (.out(STEP_out));
  Clock OSC (.out(OSC_out));
  LED D7 (.in(counter_1_q[7]));
  assign W_BUS = PC_OUT ? counter_1_q : 8'bz;  // Controlled_Buffer controlled_buffer_1
  Counter counter_1 (.load(JMP), .D(W_BUS), .count(PC_INC), .Q(counter_1_q), .clk(CLK), .clr(RESET));  // open: carry
  LED D7_2 (.in(register_1_q[7]));
  Register register_1 (.D(W_BUS), .en(ADDR_IN), .Q(register_1_q), .clk(CLK), .clr(RESET));
  LED D7_3 (.in(ram_1_data[7]));
  LED D6 (.in(counter_1_q[6]));
  LED D4 (.in(counter_1_q[4]));
  LED D3 (.in(counter_1_q[3]));
  LED D5 (.in(counter_1_q[5]));
  LED D5_2 (.in(register_1_q[5]));
  LED D3_2 (.in(register_1_q[3]));
  LED D6_2 (.in(register_1_q[6]));
  LED D4_2 (.in(register_1_q[4]));
  LED D6_3 (.in(ram_1_data[6]));
  LED D5_3 (.in(ram_1_data[5]));
  LED D4_3 (.in(ram_1_data[4]));
  LED D3_3 (.in(ram_1_data[3]));
  RAM ram_1 (.addr(register_1_q), .data(ram_1_data), .clk(CLK), .ld(not_1_out));  // open: sel, clr
  not not_1 (not_1_out, RAM_IN);
  T_Flip_Flop t_ff_1 (.clk(RUN_out), .T(1'b1), .Q(RUN), .reset(RESET), .en(1'b1));  // open: Qn, preset
  and and_1 (and_1_out, STEP_out, ~RUN);  // AND_Gate
  or or_1 (or_1_out, and_1_out, and_2_out);
  and and_2 (and_2_out, RUN, OSC_out);
  nor nor_1 (nor_1_out, C_OUT, S_OUT);
  xor xor_1 (xor_1_out, C, FLAG_INV);
  xor xor_2 (xor_2_out, Z, FLAG_INV);
  xor xor_3 (xor_3_out, S, FLAG_INV);
  LED D2 (.in(counter_1_q[2]));
  LED D1 (.in(counter_1_q[1]));
  LED D0 (.in(counter_1_q[0]));
  LED D0_2 (.in(register_1_q[0]));
  LED D1_2 (.in(register_1_q[1]));
  LED D2_2 (.in(register_1_q[2]));
  LED D2_3 (.in(ram_1_data[2]));
  LED D1_3 (.in(ram_1_data[1]));
  LED D0_3 (.in(ram_1_data[0]));
  assign W_BUS = RAM_OUT ? ram_1_data : 8'bz;  // Controlled_Buffer controlled_buffer_2
  assign ram_1_data = RAM_IN ? W_BUS : 8'bz;  // Controlled_Buffer controlled_buffer_3
  and and_3 (CLK, or_1_out, ~HALT);  // AND_Gate
  and and_4 (and_4_out, PC_IN, nor_1_out);
  and and_5 (and_5_out, PC_IN, and_6_out);
  and and_6 (and_6_out, C_OUT, xor_1_out);
  and and_7 (and_7_out, PC_IN, and_8_out);
  and and_8 (and_8_out, Z_OUT, xor_2_out);
  and and_9 (and_9_out, PC_IN, and_10_out);
  and and_10 (and_10_out, S_OUT, xor_3_out);
  or or_2 (JMP, and_4_out, and_5_out, and_7_out, and_9_out);
  LED D4_4 (.in(W_BUS[4]));
  LED D7_4 (.in(W_BUS[7]));
  LED D5_4 (.in(W_BUS[5]));
  LED D6_4 (.in(W_BUS[6]));
  LED D0_4 (.in(W_BUS[0]));
  LED D2_4 (.in(W_BUS[2]));
  LED D1_4 (.in(W_BUS[1]));
  LED D3_4 (.in(W_BUS[3]));
  Counter #(.width(3), .max('h7)) counter_2 (.Q(T_STATE), .clk(CLK), .clr(or_3_out));  // open: load, D, count, carry
  or or_3 (or_3_out, T_RESET, RESET);
  Register register_2 (.D(W_BUS), .en(IR_IN), .Q(IR_REG), .clk(CLK), .clr(RESET));
  assign W_BUS = A_OUT ? A_BUS : 8'bz;  // Controlled_Buffer controlled_buffer_4
  Register register_3 (.D(W_BUS), .en(A_IN), .Q(A_BUS), .clk(CLK), .clr(RESET));
  assign W_BUS = B_OUT ? register_4_q : 8'bz;  // Controlled_Buffer controlled_buffer_5
  Register register_4 (.D(W_BUS), .en(B_IN), .Q(register_4_q), .clk(CLK), .clr(RESET));
  LED T0 (.in(decoder_1_out0));
  LED T1 (.in(decoder_1_out1));
  LED D6_5 (.in(IR_REG[6]));
  LED D7_5 (.in(IR_REG[7]));
  LED D7_6 (.in(A_BUS[7]));
  LED D6_6 (.in(A_BUS[6]));
  LED D6_7 (.in(register_4_q[6]));
  LED D7_7 (.in(register_4_q[7]));
  LED led_1 (.in(CLK));
  Decoder #(.select(3)) decoder_1 (
    .out0(decoder_1_out0), .out1(decoder_1_out1), .out2(T2), .out3(decoder_1_out3), .out4(decoder_1_out4),
    .out5(decoder_1_out5), .out6(decoder_1_out6), .out7(decoder_1_out7), .sel(T_STATE));  // open: en
  LED T4 (.in(decoder_1_out4));
  LED T3 (.in(decoder_1_out3));
  LED T5 (.in(decoder_1_out5));
  LED u_T2 (.in(T2));
  LED D2_5 (.in(IR_REG[2]));
  LED D3_5 (.in(IR_REG[3]));
  LED D5_5 (.in(IR_REG[5]));
  LED D4_5 (.in(IR_REG[4]));
  LED D4_6 (.in(A_BUS[4]));
  LED D3_6 (.in(A_BUS[3]));
  LED D2_6 (.in(A_BUS[2]));
  LED D5_6 (.in(A_BUS[5]));
  LED D2_7 (.in(register_4_q[2]));
  LED D3_7 (.in(register_4_q[3]));
  LED D4_7 (.in(register_4_q[4]));
  LED D5_7 (.in(register_4_q[5]));
  LED led_2 (.in(RUN));
  LED T7 (.in(decoder_1_out7));
  LED T6 (.in(decoder_1_out6));
  LED D0_5 (.in(IR_REG[0]));
  LED D1_5 (.in(IR_REG[1]));
  LED D0_6 (.in(A_BUS[0]));
  LED D1_6 (.in(A_BUS[1]));
  LED D1_7 (.in(register_4_q[1]));
  LED D0_7 (.in(register_4_q[0]));
  LED led_3 (.in(PC_OUT));
  LED led_4 (.in(PC_INC));
  LED led_5 (.in(RAM_OUT));
  LED led_6 (.in(HALT));
  LED led_7 (.in(PC_IN));
  LED led_8 (.in(ADDR_IN));
  LED led_9 (.in(RAM_IN));
  LED led_10 (.in(IR_IN));
  Counter #(.width(2), .max('h3)) counter_3 (.Q(MODE), .clk(MODE_out));  // open: load, D, count, carry, clr
  assign W_BUS = TMP_OUT ? register_6_q : 8'bz;  // Controlled_Buffer controlled_buffer_6
  and and_11 (and_11_out, C, C_OUT);
  Register register_5 (.D(W_BUS), .en(DISP_IN), .Q(register_5_q), .clk(CLK), .clr(RESET));
  Button u_MODE (.out(MODE_out));
  Register register_6 (.D(controlled_buffer_7_out), .en(ALU_OUT), .Q(register_6_q), .clk(CLK), .clr(RESET));
  D_Flip_Flop d_ff_1 (.clk(CLK), .D(ALU_C), .Q(C), .preset(ALU_STC), .en(ALU_OUT), .reset(or_4_out));  // open: Qn
  or or_4 (or_4_out, RESET, ALU_CLC);
  Adder adder_1 (.a(A_BUS), .b(W_BUS), .out(adder_1_out), .cin(and_11_out), .cout(adder_1_cout[8]));
  Subtractor subtractor_1 (.a(A_BUS), .b(W_BUS), .out(subtractor_1_out), .bin(and_11_out), .bout(subtractor_1_bout[8]));
  LED led_11 (.in(ALU_OUT));
  LED led_12 (.in(C_OUT));
  LED led_13 (.in(Z_OUT));
  LED led_14 (.in(S_OUT));
  _7_Segment_Display u_7_segment_display_1 (
    .g(rom_2_data_3[7]), .f(rom_2_data_3[6]), .a(rom_2_data_3[5]), .b(rom_2_data_3[4]), .e(rom_2_data_2[3]),
    .d(rom_2_data_2[2]), .c(rom_2_data_2[1]), .dp(rom_2_data_2[0]));
  _7_Segment_Display u_7_segment_display_2 (
    .g(rom_2_data_5[7]), .f(rom_2_data_5[6]), .a(rom_2_data_5[5]), .b(rom_2_data_5[4]), .e(rom_2_data_4[3]),
    .d(rom_2_data_4[2]), .c(rom_2_data_4[1]), .dp(rom_2_data_4[0]));
  LED D4_8 (.in(register_6_q[4]));
  LED D6_8 (.in(register_6_q[6]));
  LED D7_8 (.in(register_6_q[7]));
  LED D5_8 (.in(register_6_q[5]));
  LED D6_9 (.in(multiplexer_1_out[6]));
  LED D4_9 (.in(ALU_S));
  LED D5_9 (.in(multiplexer_1_out[5]));
  LED D7_9 (.in(multiplexer_1_out[7]));
  assign controlled_buffer_7_out = ALU_OUT ? {multiplexer_1_out[7:5], ALU_S, multiplexer_1_out[3:0]} : 8'bz;  // Controlled_Buffer controlled_buffer_7
  LED led_15 (.in(ALU_SUB));
  LED led_16 (.in(ALU_STC));
  LED led_17 (.in(ALU_CLC));
  LED led_18 (.in(FLAG_INV));
  _7_Segment_Display u_7_segment_display_3 (
    .g(rom_2_data[15]), .f(rom_2_data[14]), .a(rom_2_data[13]), .b(rom_2_data[12]), .e(rom_2_data[11]),
    .d(rom_2_data[10]), .c(rom_2_data[9]), .dp(rom_2_data[8]));
  LED D0_8 (.in(register_6_q[0]));
  LED D3_8 (.in(register_6_q[3]));
  LED D1_8 (.in(register_6_q[1]));
  LED D2_8 (.in(register_6_q[2]));
  Register #(.width(1)) register_7 (.D(ALU_Z), .en(ALU_OUT), .Q(Z), .clk(CLK), .clr(RESET));
  LED D2_9 (.in(multiplexer_1_out[2]));
  LED D3_9 (.in(multiplexer_1_out[3]));
  LED D0_9 (.in(multiplexer_1_out[0]));
  LED D1_9 (.in(multiplexer_1_out[1]));
  Multiplexer #(.width(9)) multiplexer_1 (
    .in0({adder_1_cout[8], adder_1_out}), .in1({subtractor_1_bout[8], subtractor_1_out}),
    .out({ALU_C, multiplexer_1_out[7:5], ALU_S, multiplexer_1_out[3:0]}), .sel(ALU_SUB));  // open: en
  ROM #(.addrWidth(12), .dataWidth(24)) rom_1 (
    .addr({IR_REG, 1'b0, T_STATE}),
    .data({T_RESET, ALU_SUB, ALU_CLC, ALU_STC, FLAG_INV, S_OUT, Z_OUT, C_OUT, DISP_IN, ALU_OUT, TMP_IN, TMP_OUT, B_IN, B_OUT, A_IN, A_OUT, IR_IN, HALT, RAM_IN, RAM_OUT, ADDR_IN, PC_INC, PC_IN, PC_OUT}));  // open: sel
  ROM #(.addrWidth(10), .dataWidth(32)) rom_2 (
    .addr({MODE, register_5_q}), .data({rom_2_data_5, rom_2_data_4, rom_2_data_3, rom_2_data_2, rom_2_data}));  // open: sel
  _7_Segment_Display u_7_segment_display_4 (
    .g(rom_2_data[7]), .f(rom_2_data[6]), .a(rom_2_data[5]), .b(rom_2_data[4]), .e(rom_2_data[3]),
    .d(rom_2_data[2]), .c(rom_2_data[1]), .dp(rom_2_data[0]));
  LED u_S (.in(S));
  LED u_Z (.in(Z));
  LED u_C (.in(C));
  LED S_2 (.in(ALU_S));
  LED C_2 (.in(ALU_C));
  LED Z_2 (.in(ALU_Z));
  nor nor_2 (ALU_Z, multiplexer_1_out[3], multiplexer_1_out[2], multiplexer_1_out[1], multiplexer_1_out[0], multiplexer_1_out[7], multiplexer_1_out[6], multiplexer_1_out[5], ALU_S);
  LED led_19 (.in(A_OUT));
  LED led_20 (.in(B_OUT));
  LED led_21 (.in(TMP_OUT));
  Decoder #(.select(2)) decoder_2 (.out0(UNSIGNED), .out1(SIGNED), .out2(HEX), .out3(OCTAL), .sel(MODE));  // open: en
  LED led_22 (.in(UNSIGNED));
  LED led_23 (.in(SIGNED));
  LED led_24 (.in(HEX));
  LED led_25 (.in(OCTAL));
  Register #(.width(1)) register_8 (.D(ALU_S), .en(ALU_OUT), .Q(S), .clk(CLK), .clr(RESET));
  LED led_26 (.in(A_IN));
  LED led_27 (.in(B_IN));
  LED led_28 (.in(TMP_IN));
  LED led_29 (.in(DISP_IN));

  // Notes on the sheet:
  //   256 BYTE RAM
  //   PROGRAM COUNTER
  //   ADDRESS REGISTER
  //   RAM
  //   JUMP LOGIC
  //   W BUS
  //   T STATE
  //   INSTRUCTION REGISTER
  //   A REG
  //   B REG
  //   CONTROL SIGNALS
  //   DISPLAY DECODER ROM
  //   TMP REG
  //   ALU
  //   INSTRUCTION DECODER ROM
  //   contents of rom_1 (hex, n*v repeats v):
  //   9 94 9 1c 210 800000 800000 800000 8*ffffff 9 94 9 1c 810 800000 800000 800000 8*ffffff 9 94
  //   6*800000 8*ffffff 9 94 6*800000 8*ffffff 9 94 9 214 4*800000 8*ffffff 9 94 9 814 4*800000 8*ffffff 9
  //   94 6*800000 8*ffffff 9 94 6*800000 8*ffffff 9 94 9 1c 120 800000 800000 800000 8*ffffff 9 94 9 1c
  //   420 800000 800000 800000 8*ffffff 9 94 6*800000 8*ffffff 9 94 6*800000 8*ffffff 9 94 900 5*800000
  //   8*ffffff 9 94 600 5*800000 8*ffffff 9 94 6*800000 8*ffffff 9 94 6*800000 8*ffffff 9 94 9 1c 4010
  //   1200 800000 800000 8*ffffff 9 94 9 4010 1200 800000 800000 800000 8*ffffff 9 94 4100 1200 4*800000
  //   8*ffffff 9 94 4400 1200 4*800000 8*ffffff 9 94 9 1c 14010 1200 800000 800000 8*ffffff 9 94 9 14010
  //   1200 800000 800000 800000 8*ffffff 9 94 14100 1200 4*800000 8*ffffff 9 94 14400 1200 4*800000
  //   8*ffffff 9 94 9 1c 404010 1200 800000 800000 8*ffffff 9 94 9 404010 1200 800000 800000 800000
  //   8*ffffff 9 94 404100 1200 4*800000 8*ffffff 9 94 404400 1200 4*800000 8*ffffff 9 94 9 1c 414010 1200
  //   800000 800000 8*ffffff 9 94 9 414010 1200 800000 800000 800000 8*ffffff 9 94 414100 1200 4*800000
  //   8*ffffff 9 94 414400 1200 4*800000 8*ffffff 9 94 200000 5*800000 8*ffffff 9 94 100000 5*800000
  //   8*ffffff 9 94 6*800000 8*ffffff 9 94 6*800000 8*ffffff 9 94 6*800000 8*ffffff 9 94 6*800000 8*ffffff
  //   9 94 6*800000 8*ffffff 9 94 6*800000 8*ffffff 9 94 6*800000 8*ffffff 9 94 6*800000 8*ffffff 9 94
  //   6*800000 8*ffffff 9 94 6*800000 8*ffffff 9 94 6*800000 8*ffffff 9 94 6*800000 8*ffffff 9 94 6*800000
  //   8*ffffff 9 94 6*800000 8*ffffff 9 94 9 12 4*800000 8*ffffff 9 94 6*800000 8*ffffff 9 94 9 10012
  //   4*800000 8*ffffff 9 94 9 90012 4*800000 8*ffffff 9 94 9 10012 4*800000 8*ffffff 9 94 9 10012
  //   4*800000 8*ffffff 9 94 9 10012 4*800000 8*ffffff 9 94 9 10012 4*800000 8*ffffff 9 94 9 1c 8010
  //   800000 800000 800000 8*ffffff 9 94 9 8010 4*800000 8*ffffff 9 94 8100 5*800000 8*ffffff 9 94 8400
  //   5*800000 8*ffffff 9 94 6*800000 8*ffffff 9 94 6*800000 8*ffffff 9 94 6*800000 8*ffffff 9 94 40
  //   5*800000 8*ffffff
  //   contents of rom_2 (hex, n*v repeats v):
  //   7e 12 bc b6 d2 e6 ee 32 fe f2 127e 1212 12bc 12b6 12d2 12e6 12ee 1232 12fe 12f2 bc7e bc12 bcbc bcb6
  //   bcd2 bce6 bcee bc32 bcfe bcf2 b67e b612 b6bc b6b6 b6d2 b6e6 b6ee b632 b6fe b6f2 d27e d212 d2bc d2b6
  //   d2d2 d2e6 d2ee d232 d2fe d2f2 e67e e612 e6bc e6b6 e6d2 e6e6 e6ee e632 e6fe e6f2 ee7e ee12 eebc eeb6
  //   eed2 eee6 eeee ee32 eefe eef2 327e 3212 32bc 32b6 32d2 32e6 32ee 3232 32fe 32f2 fe7e fe12 febc feb6
  //   fed2 fee6 feee fe32 fefe fef2 f27e f212 f2bc f2b6 f2d2 f2e6 f2ee f232 f2fe f2f2 127e7e 127e12 127ebc
  //   127eb6 127ed2 127ee6 127eee 127e32 127efe 127ef2 12127e 121212 1212bc 1212b6 1212d2 1212e6 1212ee
  //   121232 1212fe 1212f2 12bc7e 12bc12 12bcbc 12bcb6 12bcd2 12bce6 12bcee 12bc32 12bcfe 12bcf2 12b67e
  //   12b612 12b6bc 12b6b6 12b6d2 12b6e6 12b6ee 12b632 12b6fe 12b6f2 12d27e 12d212 12d2bc 12d2b6 12d2d2
  //   12d2e6 12d2ee 12d232 12d2fe 12d2f2 12e67e 12e612 12e6bc 12e6b6 12e6d2 12e6e6 12e6ee 12e632 12e6fe
  //   12e6f2 12ee7e 12ee12 12eebc 12eeb6 12eed2 12eee6 12eeee 12ee32 12eefe 12eef2 12327e 123212 1232bc
  //   1232b6 1232d2 1232e6 1232ee 123232 1232fe 1232f2 12fe7e 12fe12 12febc 12feb6 12fed2 12fee6 12feee
  //   12fe32 12fefe 12fef2 12f27e 12f212 12f2bc 12f2b6 12f2d2 12f2e6 12f2ee 12f232 12f2fe 12f2f2 bc7e7e
  //   bc7e12 bc7ebc bc7eb6 bc7ed2 bc7ee6 bc7eee bc7e32 bc7efe bc7ef2 bc127e bc1212 bc12bc bc12b6 bc12d2
  //   bc12e6 bc12ee bc1232 bc12fe bc12f2 bcbc7e bcbc12 bcbcbc bcbcb6 bcbcd2 bcbce6 bcbcee bcbc32 bcbcfe
  //   bcbcf2 bcb67e bcb612 bcb6bc bcb6b6 bcb6d2 bcb6e6 bcb6ee bcb632 bcb6fe bcb6f2 bcd27e bcd212 bcd2bc
  //   bcd2b6 bcd2d2 bcd2e6 bcd2ee bcd232 bcd2fe bcd2f2 bce67e bce612 bce6bc bce6b6 bce6d2 bce6e6 7e 12 bc
  //   b6 d2 e6 ee 32 fe f2 127e 1212 12bc 12b6 12d2 12e6 12ee 1232 12fe 12f2 bc7e bc12 bcbc bcb6 bcd2 bce6
  //   bcee bc32 bcfe bcf2 b67e b612 b6bc b6b6 b6d2 b6e6 b6ee b632 b6fe b6f2 d27e d212 d2bc d2b6 d2d2 d2e6
  //   d2ee d232 d2fe d2f2 e67e e612 e6bc e6b6 e6d2 e6e6 e6ee e632 e6fe e6f2 ee7e ee12 eebc eeb6 eed2 eee6
  //   eeee ee32 eefe eef2 327e 3212 32bc 32b6 32d2 32e6 32ee 3232 32fe 32f2 fe7e fe12 febc feb6 fed2 fee6
  //   feee fe32 fefe fef2 f27e f212 f2bc f2b6 f2d2 f2e6 f2ee f232 f2fe f2f2 127e7e 127e12 127ebc 127eb6
  //   127ed2 127ee6 127eee 127e32 127efe 127ef2 12127e 121212 1212bc 1212b6 1212d2 1212e6 1212ee 121232
  //   1212fe 1212f2 12bc7e 12bc12 12bcbc 12bcb6 12bcd2 12bce6 12bcee 12bc32 8012bcfe 8012bc32 8012bcee
  //   8012bce6 8012bcd2 8012bcb6 8012bcbc 8012bc12 8012bc7e 801212f2 801212fe 80121232 801212ee 801212e6
  //   801212d2 801212b6 801212bc 80121212 8012127e 80127ef2 80127efe 80127e32 80127eee 80127ee6 80127ed2
  //   80127eb6 80127ebc 80127e12 80127e7e 8000f2f2 8000f2fe 8000f232 8000f2ee 8000f2e6 8000f2d2 8000f2b6
  //   8000f2bc 8000f212 8000f27e 8000fef2 8000fefe 8000fe32 8000feee 8000fee6 8000fed2 8000feb6 8000febc
  //   8000fe12 8000fe7e 800032f2 800032fe 80003232 800032ee 800032e6 800032d2 800032b6 800032bc 80003212
  //   8000327e 8000eef2 8000eefe 8000ee32 8000eeee 8000eee6 8000eed2 8000eeb6 8000eebc 8000ee12 8000ee7e
  //   8000e6f2 8000e6fe 8000e632 8000e6ee 8000e6e6 8000e6d2 8000e6b6 8000e6bc 8000e612 8000e67e 8000d2f2
  //   8000d2fe 8000d232 8000d2ee 8000d2e6 8000d2d2 8000d2b6 8000d2bc 8000d212 8000d27e 8000b6f2 8000b6fe
  //   8000b632 8000b6ee 8000b6e6 8000b6d2 8000b6b6 8000b6bc 8000b612 8000b67e 8000bcf2 8000bcfe 8000bc32
  //   8000bcee 8000bce6 8000bcd2 8000bcb6 8000bcbc 8000bc12 8000bc7e 800012f2 800012fe 80001232 800012ee
  //   800012e6 800012d2 800012b6 800012bc 80001212 8000127e 800000f2 800000fe 80000032 800000ee 800000e6
  //   800000d2 800000b6 800000bc 80000012 7e7e00 7e1200 7ebc00 7eb600 7ed200 7ee600 7eee00 7e3200 7efe00
  //   7ef200 7efa00 7ece00 7e6c00 7e9e00 7eec00 7ee800 127e00 121200 12bc00 12b600 12d200 12e600 12ee00
  //   123200 12fe00 12f200 12fa00 12ce00 126c00 129e00 12ec00 12e800 bc7e00 bc1200 bcbc00 bcb600 bcd200
  //   bce600 bcee00 bc3200 bcfe00 bcf200 bcfa00 bcce00 bc6c00 bc9e00 bcec00 bce800 b67e00 b61200 b6bc00
  //   b6b600 b6d200 b6e600 b6ee00 b63200 b6fe00 b6f200 b6fa00 b6ce00 b66c00 b69e00 b6ec00 b6e800 d27e00
  //   d21200 d2bc00 d2b600 d2d200 d2e600 d2ee00 d23200 d2fe00 d2f200 d2fa00 d2ce00 d26c00 d29e00 d2ec00
  //   d2e800 e67e00 e61200 e6bc00 e6b600 e6d200 e6e60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
  //   DISPLAY MODE DECODER
endmodule
